# Fritzing sketch conn_mpr121_irq (saved by Fritzing 1.0.5)

parts:
  Mod1 = Raspberry Pi 4B
  Компонент1 = MPR121 Breakout
  J1 = STARBOARD_GND [package=starboard_ground]
  J2 = STARBOARD_GND [package=starboard_ground]
  J3 = STARBOARD_GND [package=starboard_ground]

nets:
  3V3: Mod1.3V3, Компонент1.3.3V
  N1: Mod1.GPIO2, Компонент1.SDA
  N2: Mod1.GPIO3, Компонент1.SCL
  GND: Mod1.GND, Компонент1.GND
  N3: Mod1.GPIO18, Компонент1.~IRQ
  N4: Компонент1.ELE10, J1.MOUNT
  N5: Компонент1.ELE9, J2.MOUNT
  N6: Компонент1.ELE8, J3.MOUNT

notes:
  3.3V → 3.3V
  GND → GND
  GPIO 18 → IRQ
  SDA (GPIO02) → SDA
  SCL (GPIO03) → SCL
