# Fritzing sketch conn_servo_0 (saved by Fritzing 1.0.5)

parts:
  Raspberry_Pi_2 = Raspberry Pi 3 [part_number=RPI-3-V1.2]
  J2 = Basic Servo

nets:
  N1: Raspberry_Pi_2.GPIO17, J2.pulse
  GND: Raspberry_Pi_2.GND, J2.gnd
  5V: Raspberry_Pi_2.5V, J2.vcc

notes:
  5V (PIN2) → Vin
  GND (PIN6) → GND
  GPIO17 → CTR
